// Logisim project Programs.circ as structural Verilog: 3 circuits, main circuit Loader
module Loader (
  input  Clock,
  input  [7:0] PIn,
  output [9:0] out_3
);

  wire buffer_1_out, buffer_2_out, buffer_3_out, buffer_4_out, buffer_5_out, not_1_out, not_2_out, not_3_out;

  nor nor_1 (out_3[9], out_3[8], not_1_out);
  buf buffer_1 (buffer_1_out, Clock);
  buf buffer_2 (buffer_2_out, buffer_1_out);
  buf buffer_3 (buffer_3_out, buffer_2_out);
  not not_1 (not_1_out, not_2_out);
  not not_2 (not_2_out, not_3_out);
  not not_3 (not_3_out, out_3[8]);
  buf buffer_4 (buffer_4_out, buffer_3_out);
  buf buffer_5 (buffer_5_out, buffer_4_out);
  buf buffer_6 (out_3[8], buffer_5_out);

  assign out_3[7:0] = PIn;
endmodule

module Prog_incR3 (
  input  Res,
  input  Clock,
  output [7:0] out_3
);

  wire and_1_out, d_ff_1_q, nor_1_out, not_1_out, not_2_out, not_3_out;
  wire [7:0] counter_1_q;

  D_Flip_Flop d_ff_1 (.Q(d_ff_1_q), .preset(nor_1_out), .reset(Res));  // open: clk, D, Qn, en
  nor nor_1 (nor_1_out, not_1_out, Clock);
  not not_1 (not_1_out, not_2_out);
  not not_2 (not_2_out, not_3_out);
  not not_3 (not_3_out, Clock);
  Counter counter_1 (.count(1'b1), .Q(counter_1_q), .clk(and_1_out), .clr(Res));  // open: load, D, carry
  and and_1 (and_1_out, Clock, d_ff_1_q);
  ROM rom_1 (.addr(counter_1_q), .data(out_3));  // open: sel

  // Notes on the sheet:
  //   contents of rom_1 (hex, n*v repeats v):
  //   81 11 84 22 1e 34 23 4e
endmodule

module Prog_fillMem (
  input  Res,
  input  Clock,
  output [7:0] out_3
);

  wire and_1_out, d_ff_1_q, nor_1_out, not_1_out, not_2_out, not_3_out;
  wire [7:0] counter_1_q;

  D_Flip_Flop d_ff_1 (.Q(d_ff_1_q), .preset(nor_1_out), .reset(Res));  // open: clk, D, Qn, en
  nor nor_1 (nor_1_out, not_1_out, Clock);
  not not_1 (not_1_out, not_2_out);
  not not_2 (not_2_out, not_3_out);
  not not_3 (not_3_out, Clock);
  Counter counter_1 (.count(1'b1), .Q(counter_1_q), .clk(and_1_out), .clr(Res));  // open: load, D, carry
  and and_1 (and_1_out, Clock, d_ff_1_q);
  ROM rom_1 (.addr(counter_1_q), .data(out_3));  // open: sel

  // Notes on the sheet:
  //   contents of rom_1 (hex, n*v repeats v):
  //   81 11 22 23 58 91 22 2c 44 1e 34 22 23 58 85 22 4e
endmodule
