// Logisim project SyzygyA100.circ as structural Verilog: 20 circuits, main circuit main
module main (
  input  [3:0] in_1,
  input  [3:0] in_2,
  input  Power,
  output [7:0] out_4
);

  wire and_1_out, button_2_out, button_3_out, button_4_out, button_out, clock_1_out,
       instruction_decoder_1_alu, instruction_decoder_1_alu_ng, instruction_decoder_1_jmp,
       instruction_decoder_1_lda, instruction_decoder_1_ldb, instruction_decoder_1_memr,
       instruction_decoder_1_memw, instruction_decoder_1_rd0, instruction_decoder_1_rd1,
       instruction_decoder_1_rd2, instruction_decoder_1_rd3, instruction_decoder_1_sdir,
       instruction_decoder_1_wr0, instruction_decoder_1_wr1, instruction_decoder_1_wr2,
       instruction_decoder_1_wr3, pulse_former_1_out_2, R_out;
  wire [1:0] instruction_decoder_1_alu_op;
  wire [7:0] alu_1_out, instruction_decoder_1_data_out, instruction_register_1_instr_out, mem_256_1_out_6,
       multiplexer_1_out, or_1_out, or_2_out, or_3_out, or_4_out, or_5_out, prog_fillmem_1_out_3, R0_out_6,
       R1_out_6, R2_out_6, R3_out_6;
  wire [9:0] loader_1_out_3;

  Clock clock_1 (.out(clock_1_out));
  Pulse_Former pulse_former_1 (.in_1(clock_1_out), .out_2(pulse_former_1_out_2));
  Loader loader_1 (.Clock(clock_1_out), .PIn(prog_fillmem_1_out_3), .out_3(loader_1_out_3));
  Prog_fillMem prog_fillmem_1 (.out_3(prog_fillmem_1_out_3), .Clock(clock_1_out), .Res(R_out));
  Instruction_Register instruction_register_1 (
    .Jump_Addr(R2_out_6), .Jump(instruction_decoder_1_jmp), .Instr_Out(instruction_register_1_instr_out),
    .Current_Location(out_4), .in_5(button_out), .in_9(button_2_out), .Clear(R_out), .Instr({in_1, in_2}),
    .Set(button_3_out), .EN_Out(Power), .Reset(button_4_out), .OpOut(clock_1_out),
    .Inc(pulse_former_1_out_2), .Loader_Input(loader_1_out_3));
  Button R (.out(R_out));
  Button button (.out(button_out));
  Button button_2 (.out(button_2_out));
  Mem_256 mem_256_1 (
    .in_1(R2_out_6), .in_4(R0_out_6), .out_6(mem_256_1_out_6), .Wr(and_1_out),
    .Rd(instruction_decoder_1_memr), .Clr(R_out));
  Button button_3 (.out(button_3_out));
  and and_1 (and_1_out, pulse_former_1_out_2, instruction_decoder_1_memw);
  // Probe on instruction_register_1_instr_out
  Instruction_Decoder instruction_decoder_1 (
    .in_1(instruction_register_1_instr_out), .Jmp(instruction_decoder_1_jmp),
    .Data_Out(instruction_decoder_1_data_out), .Lda(instruction_decoder_1_lda),
    .ALU(instruction_decoder_1_alu), .ALU_Op(instruction_decoder_1_alu_op),
    .SDir(instruction_decoder_1_sdir), .MemR(instruction_decoder_1_memr),
    .ALU_Ng(instruction_decoder_1_alu_ng), .wr0(instruction_decoder_1_wr0), .wr1(instruction_decoder_1_wr1),
    .wr2(instruction_decoder_1_wr2), .wr3(instruction_decoder_1_wr3), .rd0(instruction_decoder_1_rd0),
    .rd1(instruction_decoder_1_rd1), .rd2(instruction_decoder_1_rd2), .rd3(instruction_decoder_1_rd3),
    .Ldb(instruction_decoder_1_ldb), .R0(R0_out_6), .Clk(pulse_former_1_out_2),
    .MemW(instruction_decoder_1_memw));  // open: RD, WR, Mem, Ext
  Button button_4 (.out(button_4_out));
  ALU alu_1 (
    .A(or_5_out), .in_3(instruction_decoder_1_alu_ng), .Out(alu_1_out), .Op(instruction_decoder_1_alu_op),
    .Wr_A(instruction_decoder_1_lda), .Wr_B(instruction_decoder_1_ldb), .RSft(instruction_decoder_1_sdir),
    .Clk(pulse_former_1_out_2), .Rs(R_out), .Out_EN(instruction_decoder_1_alu));
  Hex_Digit_Display hex_digit_display_1 ();  // open: value, dp
  Hex_Digit_Display hex_digit_display_2 ();  // open: value, dp
  assign or_1_out = instruction_decoder_1_data_out | R1_out_6 | R2_out_6 | R3_out_6 | alu_1_out;  // OR_Gate or_1, 8 bits wide
  assign or_2_out = R0_out_6 | R2_out_6 | R3_out_6;  // OR_Gate or_2, 8 bits wide
  assign or_3_out = R0_out_6 | R1_out_6 | R3_out_6;  // OR_Gate or_3, 8 bits wide
  assign or_4_out = R0_out_6 | R1_out_6 | R2_out_6;  // OR_Gate or_4, 8 bits wide
  Register__x8 R0 (
    .in_2(multiplexer_1_out), .in_3(pulse_former_1_out_2), .out_6(R0_out_6),
    .in_1(instruction_decoder_1_rd0), .in_4(instruction_decoder_1_wr0), .in_5(R_out));
  Multiplexer #(.width(8), .enable("false")) multiplexer_1 (
    .in0(or_1_out), .in1(mem_256_1_out_6), .out(multiplexer_1_out), .sel(instruction_decoder_1_memr));
  Register__x8 R1 (
    .in_2(or_2_out), .in_3(pulse_former_1_out_2), .out_6(R1_out_6), .in_1(instruction_decoder_1_rd1),
    .in_4(instruction_decoder_1_wr1), .in_5(R_out));
  Register__x8 R2 (
    .in_2(or_3_out), .in_3(pulse_former_1_out_2), .out_6(R2_out_6), .in_1(instruction_decoder_1_rd2),
    .in_4(instruction_decoder_1_wr2), .in_5(R_out));
  Register__x8 R3 (
    .in_2(or_4_out), .in_3(pulse_former_1_out_2), .out_6(R3_out_6), .in_1(instruction_decoder_1_rd3),
    .in_4(instruction_decoder_1_wr3), .in_5(R_out));
  assign or_5_out = R3_out_6 | R2_out_6 | R1_out_6 | R0_out_6;  // OR_Gate or_5, 8 bits wide
endmodule

module Full_Adder__x1 (
  input  in_1,
  input  in_2,
  input  in_3,
  output out_4,
  output out_5
);

  wire and_1_out, and_2_out, xor_1_out;

  and and_1 (and_1_out, in_2, in_3);
  xor xor_1 (xor_1_out, in_2, in_3);
  or or_1 (out_5, and_1_out, and_2_out);
  and and_2 (and_2_out, xor_1_out, in_1);
  xor xor_2 (out_4, xor_1_out, in_1);
endmodule

module Full_Adder__x8 (
  input  [7:0] in_1,
  input  in_2,
  input  [7:0] in_3,
  output [7:0] out_4,
  output out_5
);

  wire full_adder_x1_1_out_5, full_adder_x1_2_out_5, full_adder_x1_3_out_5, full_adder_x1_4_out_5,
       full_adder_x1_5_out_5, full_adder_x1_6_out_5, full_adder_x1_7_out_5;

  Full_Adder__x1 full_adder_x1_1 (
    .in_2(in_3[0]), .in_3(in_1[0]), .out_4(out_4[0]), .in_1(in_2), .out_5(full_adder_x1_1_out_5));
  Full_Adder__x1 full_adder_x1_2 (
    .in_2(in_3[1]), .in_3(in_1[1]), .out_4(out_4[1]), .in_1(full_adder_x1_1_out_5),
    .out_5(full_adder_x1_2_out_5));
  Full_Adder__x1 full_adder_x1_3 (
    .in_2(in_3[2]), .in_3(in_1[2]), .out_4(out_4[2]), .in_1(full_adder_x1_2_out_5),
    .out_5(full_adder_x1_3_out_5));
  Full_Adder__x1 full_adder_x1_4 (
    .in_2(in_3[3]), .in_3(in_1[3]), .out_4(out_4[3]), .in_1(full_adder_x1_3_out_5),
    .out_5(full_adder_x1_4_out_5));
  Full_Adder__x1 full_adder_x1_5 (
    .in_2(in_3[4]), .in_3(in_1[4]), .out_4(out_4[4]), .in_1(full_adder_x1_4_out_5),
    .out_5(full_adder_x1_5_out_5));
  Full_Adder__x1 full_adder_x1_6 (
    .in_2(in_3[5]), .in_3(in_1[5]), .out_4(out_4[5]), .in_1(full_adder_x1_5_out_5),
    .out_5(full_adder_x1_6_out_5));
  Full_Adder__x1 full_adder_x1_7 (
    .in_2(in_3[6]), .in_3(in_1[6]), .out_4(out_4[6]), .in_1(full_adder_x1_6_out_5),
    .out_5(full_adder_x1_7_out_5));
  Full_Adder__x1 full_adder_x1_8 (
    .in_2(in_3[7]), .in_3(in_1[7]), .out_4(out_4[7]), .in_1(full_adder_x1_7_out_5), .out_5(out_5));
endmodule

module And__x8 (
  input  [7:0] in_1,
  input  [7:0] in_2,
  output [7:0] out_3
);

  and and_1 (out_3[0], in_1[0], in_2[0]);
  and and_2 (out_3[1], in_1[1], in_2[1]);
  and and_3 (out_3[2], in_1[2], in_2[2]);
  and and_4 (out_3[3], in_1[3], in_2[3]);
  and and_5 (out_3[4], in_1[4], in_2[4]);
  and and_6 (out_3[5], in_1[5], in_2[5]);
  and and_7 (out_3[6], in_1[6], in_2[6]);
  and and_8 (out_3[7], in_1[7], in_2[7]);
endmodule

module Register__x8 (
  input  in_1,
  input  [7:0] in_2,
  input  in_3,
  input  in_4,
  input  in_5,
  output [7:0] out_6
);

  wire [7:0] d_ff_1_q;

  D_Flip_Flop d_ff_1 (.clk(in_3), .D(in_2[0]), .Q(d_ff_1_q[0]), .en(in_4), .reset(in_5));  // open: Qn, preset
  D_Flip_Flop d_ff_2 (.clk(in_3), .D(in_2[1]), .Q(d_ff_1_q[1]), .en(in_4), .reset(in_5));  // open: Qn, preset
  D_Flip_Flop d_ff_3 (.clk(in_3), .D(in_2[2]), .Q(d_ff_1_q[2]), .en(in_4), .reset(in_5));  // open: Qn, preset
  D_Flip_Flop d_ff_4 (.clk(in_3), .D(in_2[3]), .Q(d_ff_1_q[3]), .en(in_4), .reset(in_5));  // open: Qn, preset
  D_Flip_Flop d_ff_5 (.clk(in_3), .D(in_2[4]), .Q(d_ff_1_q[4]), .en(in_4), .reset(in_5));  // open: Qn, preset
  D_Flip_Flop d_ff_6 (.clk(in_3), .D(in_2[5]), .Q(d_ff_1_q[5]), .en(in_4), .reset(in_5));  // open: Qn, preset
  D_Flip_Flop d_ff_7 (.clk(in_3), .D(in_2[6]), .Q(d_ff_1_q[6]), .en(in_4), .reset(in_5));  // open: Qn, preset
  D_Flip_Flop d_ff_8 (.clk(in_3), .D(in_2[7]), .Q(d_ff_1_q[7]), .en(in_4), .reset(in_5));  // open: Qn, preset
  Buffer__x8 buffer_x8_1 (.in_1(d_ff_1_q), .out_3(out_6), .in_2(in_1));
endmodule

module Buffer__x8 (
  input  [7:0] in_1,
  input  in_2,
  output [7:0] out_3
);

  and and_1 (out_3[0], in_1[0], in_2);
  and and_2 (out_3[1], in_1[1], in_2);
  and and_3 (out_3[2], in_1[2], in_2);
  and and_4 (out_3[3], in_1[3], in_2);
  and and_5 (out_3[4], in_1[4], in_2);
  and and_6 (out_3[5], in_1[5], in_2);
  and and_7 (out_3[6], in_1[6], in_2);
  and and_8 (out_3[7], in_1[7], in_2);
endmodule

module Negator__x8 (
  input  [7:0] in_1,
  input  in_2,
  output [7:0] out_3
);

  xor xor_1 (out_3[0], in_1[0], in_2);
  xor xor_2 (out_3[1], in_1[1], in_2);
  xor xor_3 (out_3[2], in_1[2], in_2);
  xor xor_4 (out_3[3], in_1[3], in_2);
  xor xor_5 (out_3[4], in_1[4], in_2);
  xor xor_6 (out_3[5], in_1[5], in_2);
  xor xor_7 (out_3[6], in_1[6], in_2);
  xor xor_8 (out_3[7], in_1[7], in_2);
endmodule

module ALU (
  input  [1:0] Op,
  input  [7:0] A,
  input  in_3,
  input  Wr_A,
  input  Wr_B,
  input  Clk,
  input  Rs,
  input  RSft,
  input  Out_EN,
  output [7:0] Out
);

  wire [7:0] and_x8_1_out_3, kogge_stone_adder_x8_1_sum, multiplexer_1_out, negator_x8_1_out_3,
       register_x8_1_out_6, register_x8_2_out_6, shifter_x8_1_out_3;

  Register__x8 register_x8_1 (.in_2(A), .in_3(Clk), .out_6(register_x8_1_out_6), .in_1(1'b1), .in_4(Wr_A), .in_5(Rs));
  Register__x8 register_x8_2 (.in_2(A), .in_3(Clk), .out_6(register_x8_2_out_6), .in_1(1'b1), .in_4(Wr_B), .in_5(Rs));
  Kogge_Stone_Adder__x8 kogge_stone_adder_x8_1 (
    .A(register_x8_1_out_6), .B(register_x8_2_out_6), .Sum(kogge_stone_adder_x8_1_sum), .Cin(1'b0));  // open: out_5
  And__x8 and_x8_1 (.in_1(register_x8_1_out_6), .in_2(register_x8_2_out_6), .out_3(and_x8_1_out_3));
  Shifter__x8 shifter_x8_1 (.in_1(register_x8_1_out_6), .out_3(shifter_x8_1_out_3), .in_2(RSft));
  Negator__x8 negator_x8_1 (.in_1(multiplexer_1_out), .out_3(negator_x8_1_out_3), .in_2(in_3));
  Multiplexer #(.select(2), .width(8), .enable("false")) multiplexer_1 (
    .in0(register_x8_1_out_6), .in1(kogge_stone_adder_x8_1_sum), .in2(and_x8_1_out_3),
    .in3(shifter_x8_1_out_3), .out(multiplexer_1_out), .sel(Op));
  Buffer__x8 buffer_x8_1 (.in_1(negator_x8_1_out_3), .out_3(Out), .in_2(Out_EN));
endmodule

module Shifter__x8 (
  input  [7:0] in_1,
  input  in_2,
  output [7:0] out_3
);

  Multiplexer #(.enable("false")) multiplexer_1 (.in0(1'b0), .in1(in_1[1]), .out(out_3[0]), .sel(in_2));
  Multiplexer #(.enable("false")) multiplexer_2 (.in0(in_1[0]), .in1(in_1[2]), .out(out_3[1]), .sel(in_2));
  Multiplexer #(.enable("false")) multiplexer_3 (.in0(in_1[1]), .in1(in_1[3]), .out(out_3[2]), .sel(in_2));
  Multiplexer #(.enable("false")) multiplexer_4 (.in0(in_1[2]), .in1(in_1[4]), .out(out_3[3]), .sel(in_2));
  Multiplexer #(.enable("false")) multiplexer_5 (.in0(in_1[3]), .in1(in_1[5]), .out(out_3[4]), .sel(in_2));
  Multiplexer #(.enable("false")) multiplexer_6 (.in0(in_1[4]), .in1(in_1[6]), .out(out_3[5]), .sel(in_2));
  Multiplexer #(.enable("false")) multiplexer_7 (.in0(in_1[5]), .in1(in_1[7]), .out(out_3[6]), .sel(in_2));
  Multiplexer #(.enable("false")) multiplexer_8 (.in0(in_1[6]), .in1(1'b0), .out(out_3[7]), .sel(in_2));
endmodule

module Kogge_Stone_Adder__x8 (
  input  [7:0] A,
  input  Cin,
  input  [7:0] B,
  output [7:0] Sum,
  output out_5
);

  wire and_1_out, half_adder_1_out_3, half_adder_1_out_4, half_adder_2_out_3, half_adder_2_out_4,
       half_adder_3_out_3, half_adder_3_out_4, half_adder_4_out_3, half_adder_4_out_4, half_adder_5_out_3,
       half_adder_5_out_4, half_adder_6_out_3, half_adder_6_out_4, half_adder_7_out_3, half_adder_7_out_4,
       half_adder_8_out_3, half_adder_8_out_4, kogge_stone_node_1_g_out, kogge_stone_node_1_out_8,
       kogge_stone_node_1_p_out, kogge_stone_node_2_g_out, kogge_stone_node_2_out_8,
       kogge_stone_node_2_p_out, kogge_stone_node_3_g_out, kogge_stone_node_3_out_8,
       kogge_stone_node_3_p_out, kogge_stone_node_4_g_out, kogge_stone_node_4_out_8,
       kogge_stone_node_4_p_out, kogge_stone_node_5_g_out, kogge_stone_node_5_out_8,
       kogge_stone_node_5_p_out, kogge_stone_node_6_g_out, kogge_stone_node_6_out_8,
       kogge_stone_node_7_g_out, kogge_stone_node_7_out_8, kogge_stone_node_7_p_out,
       kogge_stone_node_8_g_out, kogge_stone_node_8_out_8, kogge_stone_node_8_p_out,
       kogge_stone_node_9_g_out, kogge_stone_node_9_out_8, kogge_stone_node_10_g_out,
       kogge_stone_node_10_out_8, kogge_stone_node_10_p_out, kogge_stone_node_11_g_out,
       kogge_stone_node_11_out_8, kogge_stone_node_11_p_out, kogge_stone_node_12_g_out,
       kogge_stone_node_12_out_8, kogge_stone_node_13_g_out, kogge_stone_node_13_out_8,
       kogge_stone_node_13_p_out, kogge_stone_node_14_g_out, kogge_stone_node_14_out_8,
       kogge_stone_node_14_p_out, kogge_stone_node_15_g_out, kogge_stone_node_15_out_8,
       kogge_stone_node_16_g_out, kogge_stone_node_16_out_8, kogge_stone_node_16_p_out,
       kogge_stone_node_17_g_out, kogge_stone_node_17_out_8, kogge_stone_node_18_g_out,
       kogge_stone_node_18_out_8, kogge_stone_node_18_p_out, kogge_stone_node_19_g_out,
       kogge_stone_node_19_out_8, kogge_stone_node_20_g_out, kogge_stone_node_20_out_8;

  Half_Adder half_adder_1 (.in_1(A[7]), .in_2(B[7]), .out_3(half_adder_1_out_3), .out_4(half_adder_1_out_4));
  Kogge_Stone_Node kogge_stone_node_1 (
    .G_In(half_adder_1_out_3), .P_In(half_adder_1_out_4), .Prev_G(half_adder_2_out_3),
    .Prev_P(half_adder_2_out_4), .G_Out(kogge_stone_node_1_g_out), .P_Out(kogge_stone_node_1_p_out),
    .out_8(kogge_stone_node_1_out_8), .in_5(half_adder_1_out_4));
  Kogge_Stone_Node kogge_stone_node_2 (
    .G_In(kogge_stone_node_1_g_out), .P_In(kogge_stone_node_1_p_out), .Prev_G(kogge_stone_node_7_g_out),
    .Prev_P(kogge_stone_node_7_p_out), .G_Out(kogge_stone_node_2_g_out), .P_Out(kogge_stone_node_2_p_out),
    .out_8(kogge_stone_node_2_out_8), .in_5(kogge_stone_node_1_out_8));
  Kogge_Stone_Node kogge_stone_node_3 (
    .G_In(kogge_stone_node_2_g_out), .P_In(kogge_stone_node_2_p_out), .Prev_G(kogge_stone_node_11_p_out),
    .Prev_P(kogge_stone_node_11_p_out), .G_Out(kogge_stone_node_3_g_out), .P_Out(kogge_stone_node_3_p_out),
    .out_8(kogge_stone_node_3_out_8), .in_5(kogge_stone_node_2_out_8));
  Half_Adder half_adder_2 (.in_1(A[6]), .in_2(B[6]), .out_3(half_adder_2_out_3), .out_4(half_adder_2_out_4));
  and and_1 (and_1_out, kogge_stone_node_3_p_out, Cin);
  or or_1 (out_5, kogge_stone_node_3_g_out, and_1_out);
  Kogge_Stone_Node kogge_stone_node_4 (
    .G_In(half_adder_2_out_3), .P_In(half_adder_2_out_4), .Prev_G(half_adder_3_out_3),
    .Prev_P(half_adder_3_out_4), .G_Out(kogge_stone_node_4_g_out), .P_Out(kogge_stone_node_4_p_out),
    .out_8(kogge_stone_node_4_out_8), .in_5(half_adder_2_out_4));
  Kogge_Stone_Node kogge_stone_node_5 (
    .G_In(kogge_stone_node_4_g_out), .P_In(kogge_stone_node_4_p_out), .Prev_G(kogge_stone_node_10_g_out),
    .Prev_P(kogge_stone_node_10_p_out), .G_Out(kogge_stone_node_5_g_out), .P_Out(kogge_stone_node_5_p_out),
    .out_8(kogge_stone_node_5_out_8), .in_5(kogge_stone_node_4_out_8));
  Kogge_Stone_Node kogge_stone_node_6 (
    .G_In(kogge_stone_node_5_g_out), .P_In(kogge_stone_node_5_p_out), .Prev_G(kogge_stone_node_14_g_out),
    .Prev_P(1'b0), .G_Out(kogge_stone_node_6_g_out), .out_8(kogge_stone_node_6_out_8),
    .in_5(kogge_stone_node_5_out_8));  // open: P_Out
  xor xor_1 (Sum[7], kogge_stone_node_3_out_8, kogge_stone_node_6_g_out);
  Half_Adder half_adder_3 (.in_1(A[5]), .in_2(B[5]), .out_3(half_adder_3_out_3), .out_4(half_adder_3_out_4));
  Kogge_Stone_Node kogge_stone_node_7 (
    .G_In(half_adder_3_out_3), .P_In(half_adder_3_out_4), .Prev_G(half_adder_4_out_3),
    .Prev_P(half_adder_4_out_4), .G_Out(kogge_stone_node_7_g_out), .P_Out(kogge_stone_node_7_p_out),
    .out_8(kogge_stone_node_7_out_8), .in_5(half_adder_3_out_4));
  Kogge_Stone_Node kogge_stone_node_8 (
    .G_In(kogge_stone_node_7_g_out), .P_In(kogge_stone_node_7_p_out), .Prev_G(kogge_stone_node_13_g_out),
    .Prev_P(kogge_stone_node_13_p_out), .G_Out(kogge_stone_node_8_g_out), .P_Out(kogge_stone_node_8_p_out),
    .out_8(kogge_stone_node_8_out_8), .in_5(kogge_stone_node_7_out_8));
  Kogge_Stone_Node kogge_stone_node_9 (
    .G_In(kogge_stone_node_8_g_out), .P_In(kogge_stone_node_8_p_out), .Prev_G(kogge_stone_node_17_g_out),
    .Prev_P(1'b0), .G_Out(kogge_stone_node_9_g_out), .out_8(kogge_stone_node_9_out_8),
    .in_5(kogge_stone_node_8_out_8));  // open: P_Out
  xor xor_2 (Sum[6], kogge_stone_node_6_out_8, kogge_stone_node_9_g_out);
  Half_Adder half_adder_4 (.in_1(A[4]), .in_2(B[4]), .out_3(half_adder_4_out_3), .out_4(half_adder_4_out_4));
  Kogge_Stone_Node kogge_stone_node_10 (
    .G_In(half_adder_4_out_3), .P_In(half_adder_4_out_4), .Prev_G(half_adder_5_out_3),
    .Prev_P(half_adder_5_out_4), .G_Out(kogge_stone_node_10_g_out), .P_Out(kogge_stone_node_10_p_out),
    .out_8(kogge_stone_node_10_out_8), .in_5(half_adder_4_out_4));
  Kogge_Stone_Node kogge_stone_node_11 (
    .G_In(kogge_stone_node_10_g_out), .P_In(kogge_stone_node_10_p_out), .Prev_G(kogge_stone_node_16_g_out),
    .Prev_P(kogge_stone_node_16_p_out), .G_Out(kogge_stone_node_11_g_out), .P_Out(kogge_stone_node_11_p_out),
    .out_8(kogge_stone_node_11_out_8), .in_5(kogge_stone_node_10_out_8));
  Kogge_Stone_Node kogge_stone_node_12 (
    .G_In(kogge_stone_node_11_g_out), .P_In(kogge_stone_node_11_p_out), .Prev_G(kogge_stone_node_19_g_out),
    .Prev_P(1'b0), .G_Out(kogge_stone_node_12_g_out), .out_8(kogge_stone_node_12_out_8),
    .in_5(kogge_stone_node_11_out_8));  // open: P_Out
  xor xor_3 (Sum[5], kogge_stone_node_9_out_8, kogge_stone_node_12_g_out);
  Half_Adder half_adder_5 (.in_1(A[3]), .in_2(B[3]), .out_3(half_adder_5_out_3), .out_4(half_adder_5_out_4));
  Kogge_Stone_Node kogge_stone_node_13 (
    .G_In(half_adder_5_out_3), .P_In(half_adder_5_out_4), .Prev_G(half_adder_6_out_3),
    .Prev_P(half_adder_6_out_4), .G_Out(kogge_stone_node_13_g_out), .P_Out(kogge_stone_node_13_p_out),
    .out_8(kogge_stone_node_13_out_8), .in_5(half_adder_5_out_4));
  Kogge_Stone_Node kogge_stone_node_14 (
    .G_In(kogge_stone_node_13_g_out), .P_In(kogge_stone_node_13_p_out), .Prev_G(kogge_stone_node_18_g_out),
    .Prev_P(kogge_stone_node_18_p_out), .G_Out(kogge_stone_node_14_g_out), .P_Out(kogge_stone_node_14_p_out),
    .out_8(kogge_stone_node_14_out_8), .in_5(kogge_stone_node_13_out_8));
  Kogge_Stone_Node kogge_stone_node_15 (
    .G_In(kogge_stone_node_14_g_out), .P_In(kogge_stone_node_14_p_out), .Prev_G(Cin), .Prev_P(1'b0),
    .G_Out(kogge_stone_node_15_g_out), .out_8(kogge_stone_node_15_out_8), .in_5(kogge_stone_node_14_out_8));  // open: P_Out
  xor xor_4 (Sum[4], kogge_stone_node_12_out_8, kogge_stone_node_15_g_out);
  Half_Adder half_adder_6 (.in_1(A[2]), .in_2(B[2]), .out_3(half_adder_6_out_3), .out_4(half_adder_6_out_4));
  Kogge_Stone_Node kogge_stone_node_16 (
    .G_In(half_adder_6_out_3), .P_In(half_adder_6_out_4), .Prev_G(half_adder_7_out_3),
    .Prev_P(half_adder_7_out_4), .G_Out(kogge_stone_node_16_g_out), .P_Out(kogge_stone_node_16_p_out),
    .out_8(kogge_stone_node_16_out_8), .in_5(half_adder_6_out_4));
  Kogge_Stone_Node kogge_stone_node_17 (
    .G_In(kogge_stone_node_16_g_out), .P_In(kogge_stone_node_16_p_out), .Prev_G(kogge_stone_node_20_g_out),
    .Prev_P(1'b0), .G_Out(kogge_stone_node_17_g_out), .out_8(kogge_stone_node_17_out_8),
    .in_5(kogge_stone_node_16_out_8));  // open: P_Out
  xor xor_5 (Sum[3], kogge_stone_node_15_out_8, kogge_stone_node_17_g_out);
  Half_Adder half_adder_7 (.in_1(A[1]), .in_2(B[1]), .out_3(half_adder_7_out_3), .out_4(half_adder_7_out_4));
  Kogge_Stone_Node kogge_stone_node_18 (
    .G_In(half_adder_7_out_3), .P_In(half_adder_7_out_4), .Prev_G(half_adder_8_out_3),
    .Prev_P(half_adder_8_out_4), .G_Out(kogge_stone_node_18_g_out), .P_Out(kogge_stone_node_18_p_out),
    .out_8(kogge_stone_node_18_out_8), .in_5(half_adder_7_out_4));
  Kogge_Stone_Node kogge_stone_node_19 (
    .G_In(kogge_stone_node_18_g_out), .P_In(kogge_stone_node_18_p_out), .Prev_G(Cin), .Prev_P(1'b0),
    .G_Out(kogge_stone_node_19_g_out), .out_8(kogge_stone_node_19_out_8), .in_5(kogge_stone_node_18_out_8));  // open: P_Out
  xor xor_6 (Sum[2], kogge_stone_node_17_out_8, kogge_stone_node_19_g_out);
  Half_Adder half_adder_8 (.in_1(A[0]), .in_2(B[0]), .out_3(half_adder_8_out_3), .out_4(half_adder_8_out_4));
  Kogge_Stone_Node kogge_stone_node_20 (
    .G_In(half_adder_8_out_3), .P_In(half_adder_8_out_4), .Prev_G(Cin), .Prev_P(1'b0),
    .G_Out(kogge_stone_node_20_g_out), .out_8(kogge_stone_node_20_out_8), .in_5(half_adder_8_out_4));  // open: P_Out
  xor xor_7 (Sum[1], kogge_stone_node_19_out_8, kogge_stone_node_20_g_out);
  xor xor_8 (Sum[0], kogge_stone_node_20_out_8, Cin);

  // Notes on the sheet:
  //   Thanks to venividiwiki.ee.virginia.edu for the reference schematic!
endmodule

module Kogge_Stone_Node (
  input  G_In,
  input  P_In,
  input  Prev_G,
  input  Prev_P,
  input  in_5,
  output G_Out,
  output P_Out,
  output out_8
);

  wire and_1_out;

  and and_1 (and_1_out, P_In, Prev_G);
  or or_1 (G_Out, G_In, and_1_out);
  and and_2 (P_Out, P_In, Prev_P);

  assign out_8 = in_5;
endmodule

module Half_Adder (
  input  in_1,
  input  in_2,
  output out_3,
  output out_4
);

  and and_1 (out_3, in_1, in_2);
  xor xor_1 (out_4, in_1, in_2);
endmodule

module Mem_16 (
  input  Wr,
  input  Rd,
  input  [3:0] in_3,
  input  [7:0] in_4,
  input  Clr,
  output [7:0] out_6
);

  wire and_1_out, and_2_out, and_3_out, and_4_out, and_5_out, and_6_out, and_7_out, and_8_out, and_9_out,
       and_10_out, and_11_out, and_12_out, and_13_out, and_14_out, and_15_out, and_16_out, and_17_out,
       and_18_out, and_19_out, and_20_out, and_21_out, and_22_out, and_23_out, and_24_out, and_25_out,
       and_26_out, and_27_out, and_28_out, and_29_out, and_30_out, and_31_out, and_32_out, decoder_1_out0,
       decoder_1_out1, decoder_1_out2, decoder_1_out3, decoder_1_out4, decoder_1_out5, decoder_1_out6,
       decoder_1_out7, decoder_1_out8, decoder_1_out9, decoder_1_out10, decoder_1_out11, decoder_1_out12,
       decoder_1_out13, decoder_1_out14, decoder_1_out15;
  wire [7:0] register_x8_1_out_6, register_x8_2_out_6, register_x8_3_out_6, register_x8_4_out_6,
       register_x8_5_out_6, register_x8_6_out_6, register_x8_7_out_6, register_x8_8_out_6,
       register_x8_9_out_6, register_x8_10_out_6, register_x8_11_out_6, register_x8_12_out_6,
       register_x8_13_out_6, register_x8_14_out_6, register_x8_15_out_6, register_x8_16_out_6;

  Decoder #(.select(4), .enable("false")) decoder_1 (
    .out0(decoder_1_out0), .out1(decoder_1_out1), .out2(decoder_1_out2), .out3(decoder_1_out3),
    .out4(decoder_1_out4), .out5(decoder_1_out5), .out6(decoder_1_out6), .out7(decoder_1_out7),
    .out8(decoder_1_out8), .out9(decoder_1_out9), .out10(decoder_1_out10), .out11(decoder_1_out11),
    .out12(decoder_1_out12), .out13(decoder_1_out13), .out14(decoder_1_out14), .out15(decoder_1_out15),
    .sel(in_3));
  and and_1 (and_1_out, Rd, decoder_1_out0);
  Register__x8 register_x8_1 (
    .in_2(in_4), .in_3(and_2_out), .out_6(register_x8_1_out_6), .in_1(and_1_out), .in_4(1'b1), .in_5(Clr));
  and and_2 (and_2_out, decoder_1_out0, Wr);
  and and_3 (and_3_out, Rd, decoder_1_out1);
  Register__x8 register_x8_2 (
    .in_2(in_4), .in_3(and_4_out), .out_6(register_x8_2_out_6), .in_1(and_3_out), .in_4(1'b1), .in_5(Clr));
  and and_4 (and_4_out, decoder_1_out1, Wr);
  and and_5 (and_5_out, Rd, decoder_1_out2);
  Register__x8 register_x8_3 (
    .in_2(in_4), .in_3(and_6_out), .out_6(register_x8_3_out_6), .in_1(and_5_out), .in_4(1'b1), .in_5(Clr));
  and and_6 (and_6_out, decoder_1_out2, Wr);
  and and_7 (and_7_out, Rd, decoder_1_out3);
  Register__x8 register_x8_4 (
    .in_2(in_4), .in_3(and_8_out), .out_6(register_x8_4_out_6), .in_1(and_7_out), .in_4(1'b1), .in_5(Clr));
  and and_8 (and_8_out, decoder_1_out3, Wr);
  and and_9 (and_9_out, Rd, decoder_1_out4);
  Register__x8 register_x8_5 (
    .in_2(in_4), .in_3(and_10_out), .out_6(register_x8_5_out_6), .in_1(and_9_out), .in_4(1'b1), .in_5(Clr));
  and and_10 (and_10_out, decoder_1_out4, Wr);
  and and_11 (and_11_out, Rd, decoder_1_out5);
  Register__x8 register_x8_6 (
    .in_2(in_4), .in_3(and_12_out), .out_6(register_x8_6_out_6), .in_1(and_11_out), .in_4(1'b1), .in_5(Clr));
  and and_12 (and_12_out, decoder_1_out5, Wr);
  and and_13 (and_13_out, Rd, decoder_1_out6);
  Register__x8 register_x8_7 (
    .in_2(in_4), .in_3(and_14_out), .out_6(register_x8_7_out_6), .in_1(and_13_out), .in_4(1'b1), .in_5(Clr));
  and and_14 (and_14_out, decoder_1_out6, Wr);
  and and_15 (and_15_out, Rd, decoder_1_out7);
  Register__x8 register_x8_8 (
    .in_2(in_4), .in_3(and_16_out), .out_6(register_x8_8_out_6), .in_1(and_15_out), .in_4(1'b1), .in_5(Clr));
  and and_16 (and_16_out, decoder_1_out7, Wr);
  and and_17 (and_17_out, Rd, decoder_1_out8);
  Register__x8 register_x8_9 (
    .in_2(in_4), .in_3(and_18_out), .out_6(register_x8_9_out_6), .in_1(and_17_out), .in_4(1'b1), .in_5(Clr));
  and and_18 (and_18_out, decoder_1_out8, Wr);
  and and_19 (and_19_out, Rd, decoder_1_out9);
  Register__x8 register_x8_10 (
    .in_2(in_4), .in_3(and_20_out), .out_6(register_x8_10_out_6), .in_1(and_19_out), .in_4(1'b1), .in_5(Clr));
  and and_20 (and_20_out, decoder_1_out9, Wr);
  and and_21 (and_21_out, Rd, decoder_1_out10);
  Register__x8 register_x8_11 (
    .in_2(in_4), .in_3(and_22_out), .out_6(register_x8_11_out_6), .in_1(and_21_out), .in_4(1'b1), .in_5(Clr));
  and and_22 (and_22_out, decoder_1_out10, Wr);
  and and_23 (and_23_out, Rd, decoder_1_out11);
  Register__x8 register_x8_12 (
    .in_2(in_4), .in_3(and_24_out), .out_6(register_x8_12_out_6), .in_1(and_23_out), .in_4(1'b1), .in_5(Clr));
  and and_24 (and_24_out, decoder_1_out11, Wr);
  and and_25 (and_25_out, Rd, decoder_1_out12);
  Register__x8 register_x8_13 (
    .in_2(in_4), .in_3(and_26_out), .out_6(register_x8_13_out_6), .in_1(and_25_out), .in_4(1'b1), .in_5(Clr));
  and and_26 (and_26_out, decoder_1_out12, Wr);
  and and_27 (and_27_out, Rd, decoder_1_out13);
  Register__x8 register_x8_14 (
    .in_2(in_4), .in_3(and_28_out), .out_6(register_x8_14_out_6), .in_1(and_27_out), .in_4(1'b1), .in_5(Clr));
  and and_28 (and_28_out, decoder_1_out13, Wr);
  and and_29 (and_29_out, Rd, decoder_1_out14);
  Register__x8 register_x8_15 (
    .in_2(in_4), .in_3(and_30_out), .out_6(register_x8_15_out_6), .in_1(and_29_out), .in_4(1'b1), .in_5(Clr));
  and and_30 (and_30_out, decoder_1_out14, Wr);
  and and_31 (and_31_out, Rd, decoder_1_out15);
  Register__x8 register_x8_16 (
    .in_2(in_4), .in_3(and_32_out), .out_6(register_x8_16_out_6), .in_1(and_31_out), .in_4(1'b1), .in_5(Clr));
  and and_32 (and_32_out, decoder_1_out15, Wr);
  Multiplexer #(.select(4), .width(8), .enable("false")) multiplexer_1 (
    .in0(register_x8_1_out_6), .in1(register_x8_2_out_6), .in2(register_x8_3_out_6),
    .in3(register_x8_4_out_6), .in4(register_x8_5_out_6), .in5(register_x8_6_out_6),
    .in6(register_x8_7_out_6), .in7(register_x8_8_out_6), .in8(register_x8_9_out_6),
    .in9(register_x8_10_out_6), .in10(register_x8_11_out_6), .in11(register_x8_12_out_6),
    .in12(register_x8_13_out_6), .in13(register_x8_14_out_6), .in14(register_x8_15_out_6),
    .in15(register_x8_16_out_6), .out(out_6), .sel(in_3));
endmodule

module Mem_256 (
  input  [7:0] in_1,
  input  Wr,
  input  Rd,
  input  [7:0] in_4,
  input  Clr,
  output [7:0] out_6
);

  wire and_1_out, and_2_out, and_3_out, and_4_out, and_5_out, and_6_out, and_7_out, and_8_out, and_9_out,
       and_10_out, and_11_out, and_12_out, and_13_out, and_14_out, and_15_out, and_16_out, and_17_out,
       and_18_out, and_19_out, and_20_out, and_21_out, and_22_out, and_23_out, and_24_out, and_25_out,
       and_26_out, and_27_out, and_28_out, and_29_out, and_30_out, and_31_out, and_32_out, decoder_1_out0,
       decoder_1_out1, decoder_1_out2, decoder_1_out3, decoder_1_out4, decoder_1_out5, decoder_1_out6,
       decoder_1_out7, decoder_1_out8, decoder_1_out9, decoder_1_out10, decoder_1_out11, decoder_1_out12,
       decoder_1_out13, decoder_1_out14, decoder_1_out15;
  wire [7:0] mem_16_1_out_6, mem_16_2_out_6, mem_16_3_out_6, mem_16_4_out_6, mem_16_5_out_6, mem_16_6_out_6,
       mem_16_7_out_6, mem_16_8_out_6, mem_16_9_out_6, mem_16_10_out_6, mem_16_11_out_6, mem_16_12_out_6,
       mem_16_13_out_6, mem_16_14_out_6, mem_16_15_out_6, mem_16_16_out_6;

  Decoder #(.select(4), .enable("false")) decoder_1 (
    .out0(decoder_1_out0), .out1(decoder_1_out1), .out2(decoder_1_out2), .out3(decoder_1_out3),
    .out4(decoder_1_out4), .out5(decoder_1_out5), .out6(decoder_1_out6), .out7(decoder_1_out7),
    .out8(decoder_1_out8), .out9(decoder_1_out9), .out10(decoder_1_out10), .out11(decoder_1_out11),
    .out12(decoder_1_out12), .out13(decoder_1_out13), .out14(decoder_1_out14), .out15(decoder_1_out15),
    .sel(in_1[7:4]));
  and and_1 (and_1_out, Rd, decoder_1_out0);
  Mem_16 mem_16_1 (.in_3(in_1[3:0]), .in_4(in_4), .out_6(mem_16_1_out_6), .Wr(and_2_out), .Rd(and_1_out), .Clr(Clr));
  and and_2 (and_2_out, decoder_1_out0, Wr);
  and and_3 (and_3_out, Rd, decoder_1_out1);
  Mem_16 mem_16_2 (.in_3(in_1[3:0]), .in_4(in_4), .out_6(mem_16_2_out_6), .Wr(and_4_out), .Rd(and_3_out), .Clr(Clr));
  and and_4 (and_4_out, decoder_1_out1, Wr);
  and and_5 (and_5_out, Rd, decoder_1_out2);
  Mem_16 mem_16_3 (.in_3(in_1[3:0]), .in_4(in_4), .out_6(mem_16_3_out_6), .Wr(and_6_out), .Rd(and_5_out), .Clr(Clr));
  and and_6 (and_6_out, decoder_1_out2, Wr);
  and and_7 (and_7_out, Rd, decoder_1_out3);
  Mem_16 mem_16_4 (.in_3(in_1[3:0]), .in_4(in_4), .out_6(mem_16_4_out_6), .Wr(and_8_out), .Rd(and_7_out), .Clr(Clr));
  and and_8 (and_8_out, decoder_1_out3, Wr);
  and and_9 (and_9_out, Rd, decoder_1_out4);
  Mem_16 mem_16_5 (.in_3(in_1[3:0]), .in_4(in_4), .out_6(mem_16_5_out_6), .Wr(and_10_out), .Rd(and_9_out), .Clr(Clr));
  and and_10 (and_10_out, decoder_1_out4, Wr);
  and and_11 (and_11_out, Rd, decoder_1_out5);
  Mem_16 mem_16_6 (.in_3(in_1[3:0]), .in_4(in_4), .out_6(mem_16_6_out_6), .Wr(and_12_out), .Rd(and_11_out), .Clr(Clr));
  and and_12 (and_12_out, decoder_1_out5, Wr);
  and and_13 (and_13_out, Rd, decoder_1_out6);
  Mem_16 mem_16_7 (.in_3(in_1[3:0]), .in_4(in_4), .out_6(mem_16_7_out_6), .Wr(and_14_out), .Rd(and_13_out), .Clr(Clr));
  and and_14 (and_14_out, decoder_1_out6, Wr);
  and and_15 (and_15_out, Rd, decoder_1_out7);
  Mem_16 mem_16_8 (.in_3(in_1[3:0]), .in_4(in_4), .out_6(mem_16_8_out_6), .Wr(and_16_out), .Rd(and_15_out), .Clr(Clr));
  and and_16 (and_16_out, decoder_1_out7, Wr);
  and and_17 (and_17_out, Rd, decoder_1_out8);
  Mem_16 mem_16_9 (.in_3(in_1[3:0]), .in_4(in_4), .out_6(mem_16_9_out_6), .Wr(and_18_out), .Rd(and_17_out), .Clr(Clr));
  and and_18 (and_18_out, decoder_1_out8, Wr);
  and and_19 (and_19_out, Rd, decoder_1_out9);
  Mem_16 mem_16_10 (
    .in_3(in_1[3:0]), .in_4(in_4), .out_6(mem_16_10_out_6), .Wr(and_20_out), .Rd(and_19_out), .Clr(Clr));
  and and_20 (and_20_out, decoder_1_out9, Wr);
  and and_21 (and_21_out, Rd, decoder_1_out10);
  Mem_16 mem_16_11 (
    .in_3(in_1[3:0]), .in_4(in_4), .out_6(mem_16_11_out_6), .Wr(and_22_out), .Rd(and_21_out), .Clr(Clr));
  and and_22 (and_22_out, decoder_1_out10, Wr);
  and and_23 (and_23_out, Rd, decoder_1_out11);
  Mem_16 mem_16_12 (
    .in_3(in_1[3:0]), .in_4(in_4), .out_6(mem_16_12_out_6), .Wr(and_24_out), .Rd(and_23_out), .Clr(Clr));
  and and_24 (and_24_out, decoder_1_out11, Wr);
  and and_25 (and_25_out, Rd, decoder_1_out12);
  Mem_16 mem_16_13 (
    .in_3(in_1[3:0]), .in_4(in_4), .out_6(mem_16_13_out_6), .Wr(and_26_out), .Rd(and_25_out), .Clr(Clr));
  and and_26 (and_26_out, decoder_1_out12, Wr);
  and and_27 (and_27_out, Rd, decoder_1_out13);
  Mem_16 mem_16_14 (
    .in_3(in_1[3:0]), .in_4(in_4), .out_6(mem_16_14_out_6), .Wr(and_28_out), .Rd(and_27_out), .Clr(Clr));
  and and_28 (and_28_out, decoder_1_out13, Wr);
  and and_29 (and_29_out, Rd, decoder_1_out14);
  Mem_16 mem_16_15 (
    .in_3(in_1[3:0]), .in_4(in_4), .out_6(mem_16_15_out_6), .Wr(and_30_out), .Rd(and_29_out), .Clr(Clr));
  and and_30 (and_30_out, decoder_1_out14, Wr);
  and and_31 (and_31_out, Rd, decoder_1_out15);
  Mem_16 mem_16_16 (
    .in_3(in_1[3:0]), .in_4(in_4), .out_6(mem_16_16_out_6), .Wr(and_32_out), .Rd(and_31_out), .Clr(Clr));
  and and_32 (and_32_out, decoder_1_out15, Wr);
  Multiplexer #(.select(4), .width(8), .enable("false")) multiplexer_1 (
    .in0(mem_16_1_out_6), .in1(mem_16_2_out_6), .in2(mem_16_3_out_6), .in3(mem_16_4_out_6),
    .in4(mem_16_5_out_6), .in5(mem_16_6_out_6), .in6(mem_16_7_out_6), .in7(mem_16_8_out_6),
    .in8(mem_16_9_out_6), .in9(mem_16_10_out_6), .in10(mem_16_11_out_6), .in11(mem_16_12_out_6),
    .in12(mem_16_13_out_6), .in13(mem_16_14_out_6), .in14(mem_16_15_out_6), .in15(mem_16_16_out_6),
    .out(out_6), .sel(in_1[7:4]));
endmodule

module Instruction_Register (
  input  [7:0] Jump_Addr,
  input  Jump,
  input  Inc,
  input  Reset,
  input  in_5,
  input  Clear,
  input  OpOut,
  input  [9:0] Loader_Input,
  input  in_9,
  input  [7:0] Instr,
  input  Set,
  input  EN_Out,
  output [7:0] Current_Location,
  output [7:0] Instr_Out
);

  wire and_1_out, and_2_out, and_3_out, and_4_out, buffer_1_out, buffer_2_out, not_1_out, not_2_out,
       not_3_out, or_1_out, or_2_out, or_3_out, or_5_out;
  wire [7:0] buffer_x8_1_out_3, or_4_out;

  and and_1 (and_1_out, OpOut, EN_Out);
  and and_2 (and_2_out, Inc, EN_Out);
  Program_Counter program_counter_1 (
    .Reverse(in_5), .Step(or_2_out), .Jump_Addr(Jump_Addr), .Count(Current_Location), .Jump_En(Jump),
    .Clear(or_1_out));
  buf buffer_1 (buffer_1_out, buffer_2_out);
  buf buffer_2 (buffer_2_out, in_5);
  or or_1 (or_1_out, Reset, Clear);
  or or_2 (or_2_out, buffer_1_out, and_2_out, and_3_out);
  and and_3 (and_3_out, or_3_out, not_1_out);
  not not_1 (not_1_out, EN_Out);
  or or_3 (or_3_out, Loader_Input[9], in_9);
  not not_2 (not_2_out, EN_Out);
  Buffer__x8 buffer_x8_1 (.in_1(or_4_out), .out_3(buffer_x8_1_out_3), .in_2(not_2_out));
  assign or_4_out = Loader_Input[7:0] | Instr;  // OR_Gate or_4, 8 bits wide
  Mem_256 mem_256_1 (
    .in_1(Current_Location), .in_4(buffer_x8_1_out_3), .out_6(Instr_Out), .Wr(and_4_out), .Rd(and_1_out),
    .Clr(Clear));
  or or_5 (or_5_out, Loader_Input[8], Set);
  and and_4 (and_4_out, or_5_out, not_3_out);
  not not_3 (not_3_out, EN_Out);
endmodule

module Program_Counter (
  input  Jump_En,
  input  Reverse,
  input  Step,
  input  Clear,
  input  [7:0] Jump_Addr,
  output [7:0] Count
);

  wire and_1_out, and_2_out, and_3_out, and_4_out, and_5_out, and_6_out, and_7_out, and_8_out, and_9_out,
       and_10_out, and_11_out, and_12_out, and_13_out, and_14_out, delay_6t_1_out_2, j_k_ff_1_qn,
       j_k_ff_2_qn, j_k_ff_3_qn, j_k_ff_4_qn, j_k_ff_5_qn, j_k_ff_6_qn, j_k_ff_7_qn, not_1_out, not_2_out,
       not_3_out, not_4_out, not_5_out, not_6_out, not_7_out, or_1_out, or_2_out, or_3_out, or_4_out,
       or_5_out, or_6_out, or_7_out, or_8_out;
  wire [7:0] buffer_x8_1_out_3;

  Delay_6T delay_6t_1 (.in_1(Jump_En), .out_2(delay_6t_1_out_2));
  Buffer__x8 buffer_x8_1 (.in_1(Jump_Addr), .out_3(buffer_x8_1_out_3), .in_2(delay_6t_1_out_2));
  not not_1 (not_1_out, Reverse);
  J_K_Flip_Flop j_k_ff_1 (
    .J(1'b1), .clk(Step), .K(1'b1), .Q(Count[0]), .Qn(j_k_ff_1_qn), .preset(buffer_x8_1_out_3[0]),
    .reset(or_1_out));  // open: en
  or or_1 (or_1_out, Jump_En, Clear);
  and and_1 (and_1_out, not_1_out, Count[0]);
  or or_2 (or_2_out, and_1_out, and_2_out);
  and and_2 (and_2_out, j_k_ff_1_qn, Reverse);
  J_K_Flip_Flop j_k_ff_2 (
    .J(or_2_out), .clk(Step), .K(or_2_out), .Q(Count[1]), .Qn(j_k_ff_2_qn), .preset(buffer_x8_1_out_3[1]),
    .reset(or_1_out));  // open: en
  not not_2 (not_2_out, Reverse);
  and and_3 (and_3_out, not_2_out, Count[0], Count[1]);
  or or_3 (or_3_out, and_3_out, and_4_out);
  and and_4 (and_4_out, j_k_ff_2_qn, j_k_ff_1_qn, Reverse);
  J_K_Flip_Flop j_k_ff_3 (
    .J(or_3_out), .clk(Step), .K(or_3_out), .Q(Count[2]), .Qn(j_k_ff_3_qn), .preset(buffer_x8_1_out_3[2]),
    .reset(or_1_out));  // open: en
  not not_3 (not_3_out, Reverse);
  and and_5 (and_5_out, not_3_out, Count[1], Count[0], Count[2]);
  and and_6 (and_6_out, j_k_ff_3_qn, j_k_ff_1_qn, j_k_ff_2_qn, Reverse);
  or or_4 (or_4_out, and_5_out, and_6_out);
  J_K_Flip_Flop j_k_ff_4 (
    .J(or_4_out), .clk(Step), .K(or_4_out), .Q(Count[3]), .Qn(j_k_ff_4_qn), .preset(buffer_x8_1_out_3[3]),
    .reset(or_1_out));  // open: en
  not not_4 (not_4_out, Reverse);
  and and_7 (and_7_out, not_4_out, Count[2], Count[1], Count[0], Count[3]);
  and and_8 (and_8_out, j_k_ff_4_qn, j_k_ff_1_qn, j_k_ff_2_qn, j_k_ff_3_qn, Reverse);
  or or_5 (or_5_out, and_7_out, and_8_out);
  J_K_Flip_Flop j_k_ff_5 (
    .J(or_5_out), .clk(Step), .K(or_5_out), .Q(Count[4]), .Qn(j_k_ff_5_qn), .preset(buffer_x8_1_out_3[4]),
    .reset(or_1_out));  // open: en
  not not_5 (not_5_out, Reverse);
  and and_9 (and_9_out, not_5_out, Count[3], Count[2], Count[1], Count[0], Count[4]);
  or or_6 (or_6_out, and_9_out, and_10_out);
  and and_10 (and_10_out, j_k_ff_5_qn, j_k_ff_1_qn, j_k_ff_2_qn, j_k_ff_3_qn, j_k_ff_4_qn, Reverse);
  J_K_Flip_Flop j_k_ff_6 (
    .J(or_6_out), .clk(Step), .K(or_6_out), .Q(Count[5]), .Qn(j_k_ff_6_qn), .preset(buffer_x8_1_out_3[5]),
    .reset(or_1_out));  // open: en
  not not_6 (not_6_out, Reverse);
  and and_11 (and_11_out, not_6_out, Count[4], Count[3], Count[2], Count[1], Count[0], Count[5]);
  or or_7 (or_7_out, and_11_out, and_12_out);
  and and_12 (and_12_out, j_k_ff_6_qn, j_k_ff_1_qn, j_k_ff_2_qn, j_k_ff_3_qn, j_k_ff_4_qn, j_k_ff_5_qn, Reverse);
  J_K_Flip_Flop j_k_ff_7 (
    .J(or_7_out), .clk(Step), .K(or_7_out), .Q(Count[6]), .Qn(j_k_ff_7_qn), .preset(buffer_x8_1_out_3[6]),
    .reset(or_1_out));  // open: en
  not not_7 (not_7_out, Reverse);
  and and_13 (and_13_out, not_7_out, Count[5], Count[4], Count[3], Count[2], Count[1], Count[0], Count[6]);
  and and_14 (and_14_out, j_k_ff_7_qn, j_k_ff_1_qn, j_k_ff_2_qn, j_k_ff_3_qn, j_k_ff_4_qn, j_k_ff_5_qn, j_k_ff_6_qn, Reverse);
  or or_8 (or_8_out, and_13_out, and_14_out);
  J_K_Flip_Flop j_k_ff_8 (
    .J(or_8_out), .clk(Step), .K(or_8_out), .Q(Count[7]), .preset(buffer_x8_1_out_3[7]), .reset(or_1_out));  // open: Qn, en
endmodule

module Instruction_Decoder (
  input  [7:0] in_1,
  input  Clk,
  input  [7:0] R0,
  output Jmp,
  output [7:0] Data_Out,
  output [1:0] ALU_Op,
  output SDir,
  output ALU_Ng,
  output Ext,
  output RD,
  output Lda,
  output Ldb,
  output WR,
  output rd1,
  output rd3,
  output wr1,
  output wr2,
  output wr3,
  output ALU,
  output Mem,
  output MemR,
  output MemW,
  output rd0,
  output rd2,
  output wr0
);

  wire _0_2_out, _0_3_out, _0_out, and_4_out, buffer_1_out, buffer_2_out, buffer_3_out, buffer_4_out,
       buffer_5_out, buffer_6_out, buffer_7_out, buffer_8_out, buffer_9_out, buffer_10_out, buffer_11_out,
       buffer_12_out, buffer_13_out, comparator_1_ng, comparator_1_zr, cpy_out, decoder_3_out0,
       decoder_3_out1, jmp_out, ldx_out, not_1_out, not_2_out, not_3_out, not_4_out, not_5_out, not_6_out,
       not_7_out, not_8_out, not_9_out, not_10_out, not_11_out, not_12_out, not_13_out, not_14_out,
       not_15_out, not_16_out, or_1_out, sys_out;
  wire [0:0] multiplexer_2_out;
  wire [2:0] multiplexer_1_out;
  wire [3:0] decoder_1_out0, decoder_2_out0;
  wire [7:0] buffer_x8_1_out_3;

  or or_1 (or_1_out, _0_out, _0_2_out, _0_3_out);
  and and_1 (Jmp, or_1_out, Clk, jmp_out);
  not not_1 (not_1_out, in_1[7]);
  Buffer__x8 buffer_x8_1 (.in_1(in_1), .out_3(buffer_x8_1_out_3), .in_2(not_1_out));
  and _0 (_0_out, buffer_x8_1_out_3[3], comparator_1_ng);
  not not_2 (not_2_out, comparator_1_ng);
  and _0_2 (_0_2_out, not_2_out, not_3_out, buffer_x8_1_out_3[1]);
  not not_3 (not_3_out, comparator_1_zr);
  and _0_3 (_0_3_out, buffer_x8_1_out_3[2], comparator_1_zr);
  Buffer__x8 buffer_x8_2 (.in_1({1'b0, in_1[6:0]}), .out_3(Data_Out), .in_2(in_1[7]));
  Comparator comparator_1 (.in_1(R0), .zr(comparator_1_zr), .ng(comparator_1_ng));
  not not_4 (not_4_out, in_1[7]);
  buf buffer_1 (buffer_1_out, not_4_out);
  not not_5 (not_5_out, buffer_x8_1_out_3[4]);
  and sys (sys_out, buffer_1_out, not_5_out, not_6_out, not_10_out);
  or or_2 (RD, ldx_out, cpy_out);
  or or_3 (rd0, multiplexer_1_out[0], MemW, jmp_out);
  buf buffer_2 (buffer_2_out, buffer_x8_1_out_3[4]);
  not not_6 (not_6_out, buffer_x8_1_out_3[5]);
  not not_7 (not_7_out, buffer_x8_1_out_3[4]);
  not not_8 (not_8_out, buffer_x8_1_out_3[6]);
  not not_9 (not_9_out, buffer_x8_1_out_3[5]);
  not not_10 (not_10_out, buffer_x8_1_out_3[6]);
  and ldx (ldx_out, buffer_2_out, not_9_out, not_8_out);
  Decoder #(.select(2), .enable("false")) decoder_1 (
    .out0(decoder_1_out0[0]), .out1(decoder_1_out0[1]), .out2(decoder_1_out0[2]), .out3(decoder_1_out0[3]),
    .sel(buffer_x8_1_out_3[3:2]));
  Multiplexer #(.width(4), .enable("false")) multiplexer_1 (
    .in0(4'b0000), .in1(decoder_1_out0), .out({rd3, multiplexer_1_out[2], rd1, multiplexer_1_out[0]}),
    .sel(RD));
  or or_4 (rd2, multiplexer_1_out[2], Mem, jmp_out);
  not not_11 (not_11_out, buffer_x8_1_out_3[4]);
  not not_12 (not_12_out, buffer_x8_1_out_3[6]);
  not not_13 (not_13_out, buffer_x8_1_out_3[6]);
  buf buffer_3 (buffer_3_out, buffer_x8_1_out_3[5]);
  buf buffer_4 (buffer_4_out, buffer_x8_1_out_3[5]);
  buf buffer_5 (buffer_5_out, buffer_x8_1_out_3[4]);
  and cpy (cpy_out, not_7_out, buffer_4_out, not_13_out);
  and u_alu (ALU, buffer_5_out, buffer_3_out, not_12_out);
  and and_2 (Lda, buffer_x8_1_out_3[1], ldx_out);
  and and_3 (Ldb, ldx_out, buffer_x8_1_out_3[0]);
  not not_14 (not_14_out, buffer_x8_1_out_3[5]);
  not not_15 (not_15_out, buffer_x8_1_out_3[4]);
  buf buffer_6 (buffer_6_out, buffer_x8_1_out_3[6]);
  buf buffer_7 (buffer_7_out, buffer_x8_1_out_3[4]);
  not not_16 (not_16_out, buffer_x8_1_out_3[5]);
  buf buffer_8 (buffer_8_out, buffer_x8_1_out_3[6]);
  and u_jmp (jmp_out, not_11_out, not_14_out, buffer_8_out);
  and u_mem (Mem, buffer_7_out, not_16_out, buffer_6_out);
  or or_5 (WR, in_1[7], cpy_out);
  or or_6 (wr0, multiplexer_2_out[0], MemR, ALU);
  buf buffer_9 (buffer_9_out, buffer_x8_1_out_3[5]);
  buf buffer_10 (buffer_10_out, buffer_x8_1_out_3[6]);
  buf buffer_11 (buffer_11_out, buffer_x8_1_out_3[4]);
  buf buffer_12 (buffer_12_out, buffer_x8_1_out_3[5]);
  buf buffer_13 (buffer_13_out, buffer_x8_1_out_3[6]);
  and and_4 (and_4_out, buffer_11_out, buffer_9_out, buffer_10_out);
  and u_ext (Ext, not_15_out, buffer_12_out, buffer_13_out);
  Decoder #(.select(2), .enable("false")) decoder_2 (
    .out0(decoder_2_out0[0]), .out1(decoder_2_out0[1]), .out2(decoder_2_out0[2]), .out3(decoder_2_out0[3]),
    .sel(buffer_x8_1_out_3[1:0]));
  Multiplexer #(.width(4), .enable("false")) multiplexer_2 (
    .in0(4'b0000), .in1(decoder_2_out0), .out({wr3, wr2, wr1, multiplexer_2_out[0]}), .sel(WR));
  Multiplexer #(.width(2), .enable("false")) multiplexer_3 (
    .in0(2'b00), .in1(buffer_x8_1_out_3[3:2]), .out(ALU_Op), .sel(ALU));
  and and_5 (SDir, ALU, buffer_x8_1_out_3[0]);
  and and_6 (ALU_Ng, ALU, buffer_x8_1_out_3[1]);
  Decoder #(.enable("false")) decoder_3 (.out0(decoder_3_out0), .out1(decoder_3_out1), .sel(buffer_x8_1_out_3[3]));
  and and_7 (MemR, Mem, decoder_3_out0);
  and and_8 (MemW, decoder_3_out1, Mem);
endmodule

module Delay_6T (
  input  in_1,
  output out_2
);

  wire buffer_1_out, buffer_2_out, buffer_3_out, buffer_5_out, buffer_6_out;

  buf buffer_1 (buffer_1_out, buffer_2_out);
  buf buffer_2 (buffer_2_out, buffer_3_out);
  buf buffer_3 (buffer_3_out, in_1);
  buf buffer_4 (out_2, buffer_5_out);
  buf buffer_5 (buffer_5_out, buffer_6_out);
  buf buffer_6 (buffer_6_out, buffer_1_out);
endmodule

module Pulse_Former (
  input  in_1,
  output out_2
);

  wire not_1_out, not_2_out, not_3_out;

  not not_1 (not_1_out, in_1);
  not not_2 (not_2_out, not_3_out);
  not not_3 (not_3_out, not_1_out);
  nor nor_1 (out_2, in_1, not_2_out);
endmodule

module Comparator (
  input  [7:0] in_1,
  output zr,
  output ng
);

  wire or_1_out, or_2_out, or_3_out, or_4_out, or_5_out, or_6_out, or_7_out;

  or or_1 (or_1_out, in_1[7], in_1[6]);
  or or_2 (or_2_out, or_1_out, or_4_out);
  or or_3 (or_3_out, in_1[3], in_1[2]);
  or or_4 (or_4_out, in_1[5], in_1[4]);
  or or_5 (or_5_out, or_3_out, or_7_out);
  or or_6 (or_6_out, or_2_out, or_5_out);
  not not_1 (zr, or_6_out);
  or or_7 (or_7_out, in_1[1], in_1[0]);

  assign ng = in_1[7];
endmodule
